// Logisim project lab1_part2.circ as structural Verilog: 2 circuits, main circuit main
module main (
  input  a,
  input  b,
  input  c,
  output f
);

  wire n7404_1_pin2, n7432_1_pin3, n7432_1_pin4, n7432_1_pin5;

  _7432 #(.ShowInternalStructure("true")) u_7432_1 (
    .pin1(a), .pin2(b), .pin3(n7432_1_pin3), .pin4(n7432_1_pin4), .pin5(n7432_1_pin5), .pin6(f));  // open: pin13, pin12, pin11, pin10, pin9, pin8
  _7404 #(.ShowInternalStructure("true")) u_7404_1 (
    .pin1(b), .pin2(n7404_1_pin2), .pin11(n7432_1_pin3), .pin10(n7432_1_pin4));  // open: pin3, pin4, pin5, pin6, pin13, pin12, pin9, pin8
  // _7408 #(.ShowInternalStructure("true")) 7408_1: pin names not known; wires that end beside it: 1'b1, c, n7404_1_pin2, n7432_1_pin5, 1'b0
endmodule

module part2_3 (
  input  b,
  input  a,
  input  c,
  output f
);

  wire n7404_1_pin2, n7404_1_pin12, n7432_1_p4;

  _7404 #(.ShowInternalStructure("true")) u_7404_1 (
    .pin1(a), .pin2(n7404_1_pin2), .pin13(b), .pin12(n7404_1_pin12));  // open: pin3, pin4, pin5, pin6, pin11, pin10, pin9, pin8
  // _7432 #(.ShowInternalStructure("true")) 7432_1: pin names not known; wires that end beside it: 1'b1, c, n7404_1_pin2, n7432_1_p4, 1'b0
  // _7408 #(.ShowInternalStructure("true")) 7408_1: pin names not known; wires that end beside it: 1'b1, n7432_1_p4, n7404_1_pin12, f, 1'b0
endmodule
