// Logisim project lab1_part3.circ as structural Verilog: 1 circuit, main circuit main
module main (
  input  x,
  input  s,
  input  y,
  output f
);

  wire and_1_out, and_2_out, not_1_out;

  not not_1 (not_1_out, s);
  and and_1 (and_1_out, s, y);
  and and_2 (and_2_out, x, not_1_out);
  or or_1 (f, and_2_out, and_1_out);
endmodule
