// Logisim project prelab1.circ as structural Verilog: 6 circuits, main circuit main
module main (
  input  x,
  input  s,
  input  y,
  output f
);

  wire n7404_1_p3, n7408_1_pin3, n7408_1_pin11;

  // _7404 #(.ShowInternalStructure("true")) 7404_1: pin names not known; wires that end beside it: 1'b1, s, n7404_1_p3, 1'b0
  _7408 #(.ShowInternalStructure("true")) u_7408_1 (
    .pin1(s), .pin2(y), .pin3(n7408_1_pin3), .pin13(n7404_1_p3), .pin12(x), .pin11(n7408_1_pin11));  // open: pin4, pin5, pin6, pin10, pin9, pin8
  // _7432 #(.ShowInternalStructure("true")) 7432_1: pin names not known; wires that end beside it: 1'b1, n7408_1_pin3, n7408_1_pin11, f, 1'b0
endmodule

module part1_3 (
  input  x,
  input  s,
  input  y
);

  _7404 #(.ShowInternalStructure("true")) u_7404_1 ();  // open: pin1, pin2, pin3, pin4, pin5, pin6, pin13, pin12, pin11, pin10, pin9, pin8
  _7408 #(.ShowInternalStructure("true")) u_7408_1 ();  // open: pin1, pin2, pin3, pin4, pin5, pin6, pin13, pin12, pin11, pin10, pin9, pin8
  _7432 #(.ShowInternalStructure("true")) u_7432_1 ();  // open: pin1, pin2, pin3, pin4, pin5, pin6, pin13, pin12, pin11, pin10, pin9, pin8
endmodule

module help (
  input  x,
  input  y,
  input  s,
  output f
);

  wire and_1_out, and_2_out, not_1_out;

  not not_1 (not_1_out, s);
  and and_1 (and_1_out, y, s);
  or or_1 (f, and_1_out, and_2_out);
  and and_2 (and_2_out, x, not_1_out);
endmodule

module part2_2 (
  input  a,
  input  b,
  input  c,
  output f
);

  wire n7404_1_pin2, n7432_1_pin3, n7432_1_pin4, n7432_1_pin5;

  _7432 #(.ShowInternalStructure("true")) u_7432_1 (
    .pin1(a), .pin2(b), .pin3(n7432_1_pin3), .pin4(n7432_1_pin4), .pin5(n7432_1_pin5), .pin6(f));  // open: pin13, pin12, pin11, pin10, pin9, pin8
  _7404 #(.ShowInternalStructure("true")) u_7404_1 (
    .pin1(b), .pin2(n7404_1_pin2), .pin11(n7432_1_pin3), .pin10(n7432_1_pin4));  // open: pin3, pin4, pin5, pin6, pin13, pin12, pin9, pin8
  // _7408 #(.ShowInternalStructure("true")) 7408_1: pin names not known; wires that end beside it: 1'b1, c, n7404_1_pin2, n7432_1_pin5, 1'b0
endmodule

module part2_3 (
  input  b,
  input  a,
  input  c,
  output f
);

  wire n7404_1_pin2, n7404_1_pin12, n7432_1_p4;

  _7404 #(.ShowInternalStructure("true")) u_7404_1 (
    .pin1(a), .pin2(n7404_1_pin2), .pin13(b), .pin12(n7404_1_pin12));  // open: pin3, pin4, pin5, pin6, pin11, pin10, pin9, pin8
  // _7432 #(.ShowInternalStructure("true")) 7432_1: pin names not known; wires that end beside it: 1'b1, c, n7404_1_pin2, n7432_1_p4, 1'b0
  // _7408 #(.ShowInternalStructure("true")) 7408_1: pin names not known; wires that end beside it: 1'b1, n7432_1_p4, n7404_1_pin12, f, 1'b0
endmodule

module part3 (
  input  x,
  input  s,
  input  y,
  output f
);

  wire and_1_out, and_2_out, not_1_out;

  not not_1 (not_1_out, s);
  and and_1 (and_1_out, s, y);
  and and_2 (and_2_out, x, not_1_out);
  or or_1 (f, and_2_out, and_1_out);
endmodule
