// Logisim project lab2_part1.circ as structural Verilog: 3 circuits, main circuit main
module main (
  input  u,
  input  v,
  input  w,
  input  x,
  input  s1,
  input  s0,
  output m
);

  mux4to1 mux4to1_1 (.In_0(u), .In_1(v), .In_2(w), .In_3(x), .Sel_1(s1), .Sel_0(s0), .Out_0(m));
endmodule

module mux2to1 (
  input  In_0,
  input  Sel,
  input  In_1,
  output Out_1
);

  wire and_1_out, and_2_out, not_1_out;

  not not_1 (not_1_out, Sel);
  and and_1 (and_1_out, Sel, In_1);
  and and_2 (and_2_out, In_0, not_1_out);
  or or_1 (Out_1, and_2_out, and_1_out);
endmodule

module mux4to1 (
  input  In_0,
  input  In_1,
  input  In_2,
  input  In_3,
  input  Sel_1,
  input  Sel_0,
  output Out_0
);

  wire mux2to1_1_out_1, mux2to1_2_out_1;

  mux2to1 mux2to1_1 (.In_0(In_0), .Sel(Sel_0), .In_1(In_1), .Out_1(mux2to1_1_out_1));
  mux2to1 mux2to1_2 (.In_0(In_2), .Sel(Sel_0), .In_1(In_3), .Out_1(mux2to1_2_out_1));
  mux2to1 mux2to1_3 (.In_0(mux2to1_1_out_1), .Sel(Sel_1), .In_1(mux2to1_2_out_1), .Out_1(Out_0));
endmodule
