// Logisim project lab4_part1.circ as structural Verilog
module D_latch (
  input  D,
  input  Clk,
  output Qa,
  output Qb
);

  wire n7400_1_pin3, n7400_1_pin11, n7404_1_p3;

  // _7404 #(.ShowInternalStructure("true")) 7404_1: pin names not known; wires that end beside it: 1'b1, D, n7404_1_p3, 1'b0
  _7400 #(.ShowInternalStructure("true")) u_7400_1 (
    .pin1(n7404_1_p3), .pin2(Clk), .pin3(n7400_1_pin3), .pin4(n7400_1_pin3), .pin5(Qa), .pin6(Qb),
    .pin13(Clk), .pin12(D), .pin11(n7400_1_pin11), .pin10(n7400_1_pin11), .pin9(Qb), .pin8(Qa));
endmodule

module master_slave_flip_flop (
  input  D,
  input  Clk,
  output out_3
);

  wire d_latch_1_qa, not_1_out;

  D_latch d_latch_1 (.D(D), .Clk(Clk), .Qa(d_latch_1_qa));  // open: Qb
  not not_1 (not_1_out, Clk);
  D_latch d_latch_2 (.D(d_latch_1_qa), .Clk(not_1_out), .Qa(out_3));  // open: Qb
endmodule
