// Logisim project lab4_part3.circ as structural Verilog
module shifter_bit (
  input  load_n,
  input  load_val,
  input  shift,
  input  Reset,
  input  Cin,
  input  CLK,
  output Sout
);

  wire multiplexer_1_out, multiplexer_2_out;

  Multiplexer #(.enable("false")) multiplexer_1 (.in0(Sout), .in1(Cin), .out(multiplexer_1_out), .sel(shift));
  Multiplexer #(.enable("false")) multiplexer_2 (
    .in0(load_val), .in1(multiplexer_1_out), .out(multiplexer_2_out), .sel(load_n));
  D_Flip_Flop d_ff_1 (.D(multiplexer_2_out), .clk(CLK), .Q(Sout), .reset(Reset));  // open: Qn, preset
endmodule

module shift_register (
  input  [7:0] load_Val,
  input  load_n,
  input  reset,
  input  Shift_right,
  input  ASR,
  input  CLK,
  output Sout,
  output [7:0] Q
);

  wire multiplexer_1_out;

  Multiplexer #(.enable("false")) multiplexer_1 (.in0(1'b0), .in1(load_Val[7]), .out(multiplexer_1_out), .sel(ASR));
  shifter_bit shifter_bit_1 (
    .load_n(load_n), .load_val(load_Val[7]), .shift(Shift_right), .Reset(reset), .Cin(multiplexer_1_out),
    .CLK(CLK), .Sout(Q[7]));
  shifter_bit shifter_bit_2 (
    .load_n(load_n), .load_val(load_Val[6]), .shift(Shift_right), .Reset(reset), .Cin(Q[7]), .CLK(CLK),
    .Sout(Q[6]));
  shifter_bit shifter_bit_3 (
    .load_n(load_n), .load_val(load_Val[5]), .shift(Shift_right), .Reset(reset), .Cin(Q[6]), .CLK(CLK),
    .Sout(Q[5]));
  shifter_bit shifter_bit_4 (
    .load_n(load_n), .load_val(load_Val[4]), .shift(Shift_right), .Reset(reset), .Cin(Q[5]), .CLK(CLK),
    .Sout(Q[4]));
  shifter_bit shifter_bit_5 (
    .load_n(load_n), .load_val(load_Val[3]), .shift(Shift_right), .Reset(reset), .Cin(Q[4]), .CLK(CLK),
    .Sout(Q[3]));
  shifter_bit shifter_bit_6 (
    .load_n(load_n), .load_val(load_Val[2]), .shift(Shift_right), .Reset(reset), .Cin(Q[3]), .CLK(CLK),
    .Sout(Q[2]));
  shifter_bit shifter_bit_7 (
    .load_n(load_n), .load_val(load_Val[1]), .shift(Shift_right), .Reset(reset), .Cin(Q[2]), .CLK(CLK),
    .Sout(Q[1]));
  shifter_bit shifter_bit_8 (
    .load_n(load_n), .load_val(load_Val[0]), .shift(Shift_right), .Reset(reset), .Cin(Q[1]), .CLK(CLK),
    .Sout(Q[0]));

  assign Sout = Q[0];
endmodule
