// Logisim project lab5.circ as structural Verilog: 16 circuits, main circuit main
module main (
  input  SW3,
  input  SW2,
  input  SW1,
  input  SW0
);

  wire hex_decoder_1_s0, hex_decoder_1_s1, hex_decoder_1_s2, hex_decoder_1_s3, hex_decoder_1_s4,
       hex_decoder_1_s5, hex_decoder_1_s6;

  HEX_DECODER hex_decoder_1 (
    .D3(SW3), .D2(SW2), .D1(SW1), .D0(SW0), .S0(hex_decoder_1_s0), .S1(hex_decoder_1_s1),
    .S2(hex_decoder_1_s2), .S3(hex_decoder_1_s3), .S4(hex_decoder_1_s4), .S5(hex_decoder_1_s5),
    .S6(hex_decoder_1_s6));
  _7_Segment_Display u_7_segment_display_1 (
    .g(hex_decoder_1_s6), .f(hex_decoder_1_s5), .a(hex_decoder_1_s0), .b(hex_decoder_1_s1),
    .e(hex_decoder_1_s4), .d(hex_decoder_1_s3), .c(hex_decoder_1_s2));  // open: dp
endmodule

module counter8 (
  input  enable,
  input  Clk,
  input  clear_b,
  output Q7,
  output Q6,
  output Q5,
  output Q4,
  output Q3,
  output Q2,
  output Q1,
  output Q0
);

  wire and_1_out, hex_decoder_1_s0, hex_decoder_1_s1, hex_decoder_1_s2, hex_decoder_1_s3, hex_decoder_1_s4,
       hex_decoder_1_s5, hex_decoder_1_s6, hex_decoder_2_s0, hex_decoder_2_s1, hex_decoder_2_s2,
       hex_decoder_2_s3, hex_decoder_2_s4, hex_decoder_2_s5, hex_decoder_2_s6;

  counter4 counter4_1 (.enable(enable), .Clk(Clk), .clear_b(clear_b), .Q3(Q3), .Q2(Q2), .Q1(Q1), .Q0(Q0));
  HEX_DECODER hex_decoder_1 (
    .D3(Q7), .D2(Q6), .D1(Q5), .D0(Q4), .S0(hex_decoder_1_s0), .S1(hex_decoder_1_s1), .S2(hex_decoder_1_s2),
    .S3(hex_decoder_1_s3), .S4(hex_decoder_1_s4), .S5(hex_decoder_1_s5), .S6(hex_decoder_1_s6));
  and and_1 (and_1_out, Q3, Q2, enable, Q1, Q0);
  _7_Segment_Display u_7_segment_display_1 (
    .g(hex_decoder_1_s6), .f(hex_decoder_1_s5), .a(hex_decoder_1_s0), .b(hex_decoder_1_s1),
    .e(hex_decoder_1_s4), .d(hex_decoder_1_s3), .c(hex_decoder_1_s2));  // open: dp
  counter4 counter4_2 (.enable(and_1_out), .Clk(Clk), .clear_b(clear_b), .Q3(Q7), .Q2(Q6), .Q1(Q5), .Q0(Q4));
  HEX_DECODER hex_decoder_2 (
    .D3(Q3), .D2(Q2), .D1(Q1), .D0(Q0), .S0(hex_decoder_2_s0), .S1(hex_decoder_2_s1), .S2(hex_decoder_2_s2),
    .S3(hex_decoder_2_s3), .S4(hex_decoder_2_s4), .S5(hex_decoder_2_s5), .S6(hex_decoder_2_s6));
  _7_Segment_Display u_7_segment_display_2 (
    .g(hex_decoder_2_s6), .f(hex_decoder_2_s5), .a(hex_decoder_2_s0), .b(hex_decoder_2_s1),
    .e(hex_decoder_2_s4), .d(hex_decoder_2_s3), .c(hex_decoder_2_s2));  // open: dp
endmodule

module counter2 (
  input  enable,
  input  Clk,
  input  clear_b,
  output Q0,
  output Q1
);

  wire and_1_out, and_2_out, not_1_out;

  not not_1 (not_1_out, clear_b);
  T_Flip_Flop t_ff_1 (.T(enable), .clk(Clk), .Q(Q0), .reset(and_1_out));  // open: Qn, preset
  and and_1 (and_1_out, Clk, not_1_out);
  and and_2 (and_2_out, enable, Q0);
  T_Flip_Flop t_ff_2 (.T(and_2_out), .clk(Clk), .Q(Q1), .reset(and_1_out));  // open: Qn, preset
endmodule

module counter4 (
  input  enable,
  input  Clk,
  input  clear_b,
  output Q3,
  output Q2,
  output Q1,
  output Q0
);

  wire and_1_out;

  counter2 counter2_1 (.enable(enable), .Clk(Clk), .clear_b(clear_b), .Q0(Q0), .Q1(Q1));
  and and_1 (and_1_out, enable, Q0, Q1);
  counter2 counter2_2 (.enable(and_1_out), .Clk(Clk), .clear_b(clear_b), .Q0(Q2), .Q1(Q3));
endmodule

module HEX0 (
  input  D3,
  input  D2,
  input  D1,
  input  D0,
  output S0
);

  wire and_1_out, and_2_out, and_3_out, and_4_out, and_5_out, not_1_out, not_2_out, not_3_out, not_4_out;

  not not_1 (not_1_out, D3);
  not not_2 (not_2_out, D2);
  not not_3 (not_3_out, D1);
  not not_4 (not_4_out, D0);
  and and_1 (and_1_out, not_2_out, not_4_out);
  and and_2 (and_2_out, not_1_out, D1);
  and and_3 (and_3_out, not_1_out, D2, D0);
  and and_4 (and_4_out, D2, D1);
  and and_5 (and_5_out, D3, not_2_out, not_3_out);
  or or_1 (S0, and_1_out, and_2_out, and_3_out, and_4_out, and_5_out);
endmodule

module HEX1 (
  input  D3,
  input  D2,
  input  D1,
  input  D0,
  output S1
);

  wire and_1_out, and_2_out, and_3_out, and_4_out, and_5_out, not_1_out, not_2_out, not_3_out, not_4_out;

  not not_1 (not_1_out, D3);
  not not_2 (not_2_out, D2);
  not not_3 (not_3_out, D1);
  not not_4 (not_4_out, D0);
  and and_1 (and_1_out, not_1_out, not_2_out);
  and and_2 (and_2_out, not_1_out, not_3_out, not_4_out);
  and and_3 (and_3_out, not_4_out, not_2_out);
  and and_4 (and_4_out, not_1_out, D1, D0);
  and and_5 (and_5_out, D3, not_3_out, D0);
  or or_1 (S1, and_1_out, and_2_out, and_3_out, and_4_out, and_5_out);
endmodule

module HEX2 (
  input  D3,
  input  D2,
  input  D1,
  input  D0,
  output S2
);

  wire and_1_out, and_2_out, and_3_out, and_4_out, and_5_out, not_1_out, not_2_out, not_3_out;

  not not_1 (not_1_out, D3);
  not not_2 (not_2_out, D2);
  not not_3 (not_3_out, D1);
  and and_1 (and_1_out, not_1_out, D2);
  and and_2 (and_2_out, not_1_out, not_3_out);
  and and_3 (and_3_out, not_1_out, D0);
  and and_4 (and_4_out, not_3_out, D0);
  and and_5 (and_5_out, D3, not_2_out);
  or or_1 (S2, and_2_out, and_3_out, and_4_out, and_1_out, and_5_out);
endmodule

module HEX3 (
  input  D3,
  input  D2,
  input  D1,
  input  D0,
  output S3
);

  wire and_1_out, and_2_out, and_3_out, and_4_out, and_5_out, and_6_out, not_1_out, not_2_out, not_3_out,
       not_4_out;

  not not_1 (not_1_out, D3);
  not not_2 (not_2_out, D2);
  not not_3 (not_3_out, D1);
  not not_4 (not_4_out, D0);
  and and_1 (and_1_out, not_1_out, not_2_out, not_4_out);
  and and_2 (and_2_out, not_1_out, D1, not_4_out);
  and and_3 (and_3_out, not_2_out, D1, D0);
  and and_4 (and_4_out, D2, not_3_out, D0);
  and and_5 (and_5_out, D2, D1, not_4_out);
  and and_6 (and_6_out, D3, not_3_out);
  or or_1 (S3, and_1_out, and_2_out, and_3_out, and_4_out, and_5_out, and_6_out);
endmodule

module HEX4 (
  input  D3,
  input  D2,
  input  D1,
  input  D0,
  output S4
);

  wire and_1_out, and_2_out, and_3_out, and_4_out, not_1_out, not_2_out;

  not not_1 (not_1_out, D2);
  not not_2 (not_2_out, D0);
  and and_1 (and_1_out, not_1_out, not_2_out);
  and and_2 (and_2_out, D1, not_2_out);
  and and_3 (and_3_out, D3, D1);
  and and_4 (and_4_out, D3, D2);
  or or_1 (S4, and_1_out, and_2_out, and_3_out, and_4_out);
endmodule

module HEX5 (
  input  D3,
  input  D2,
  input  D1,
  input  D0,
  output S5
);

  wire and_1_out, and_2_out, and_3_out, and_4_out, and_5_out, not_1_out, not_2_out, not_3_out, not_4_out;

  not not_1 (not_1_out, D3);
  not not_2 (not_2_out, D2);
  not not_3 (not_3_out, D1);
  not not_4 (not_4_out, D0);
  and and_1 (and_1_out, not_1_out, not_3_out, not_4_out);
  and and_2 (and_2_out, not_1_out, D2, not_3_out);
  and and_3 (and_3_out, not_1_out, D2, not_4_out);
  and and_4 (and_4_out, D3, not_2_out);
  and and_5 (and_5_out, D1, D3);
  or or_1 (S5, and_1_out, and_2_out, and_3_out, and_4_out, and_5_out);
endmodule

module HEX6 (
  input  D3,
  input  D2,
  input  D1,
  input  D0,
  output S6
);

  wire and_1_out, and_2_out, and_3_out, not_1_out, not_2_out, not_3_out;

  not not_1 (not_1_out, D2);
  not not_2 (not_2_out, D1);
  not not_3 (not_3_out, D0);
  and and_1 (and_1_out, not_1_out, D1);
  and and_2 (and_2_out, not_2_out, D2);
  and and_3 (and_3_out, not_3_out, D2);
  or or_1 (S6, and_1_out, and_2_out, and_3_out, D3);
endmodule

module HEX_DECODER (
  input  D3,
  input  D2,
  input  D1,
  input  D0,
  output S0,
  output S1,
  output S2,
  output S3,
  output S4,
  output S5,
  output S6
);

  HEX0 hex0_1 (.D3(D3), .D2(D2), .D1(D1), .D0(D0), .S0(S0));
  HEX1 hex1_1 (.D3(D3), .D2(D2), .D1(D1), .D0(D0), .S1(S1));
  HEX2 hex2_1 (.D3(D3), .D2(D2), .D1(D1), .D0(D0), .S2(S2));
  HEX3 hex3_1 (.D3(D3), .D2(D2), .D1(D1), .D0(D0), .S3(S3));
  HEX4 hex4_1 (.D3(D3), .D2(D2), .D1(D1), .D0(D0), .S4(S4));
  HEX5 hex5_1 (.D3(D3), .D2(D2), .D1(D1), .D0(D0), .S5(S5));
  HEX6 hex6_1 (.D3(D3), .D2(D2), .D1(D1), .D0(D0), .S6(S6));
endmodule

module rate_divider (
  input  Reset,
  input  Enable,
  input  Clk,
  input  [1:0] Rate,
  output DivOut
);

  wire and_1_out, not_1_out, not_2_out;
  wire [7:0] counter_1_q, multiplexer_1_out;

  not not_1 (not_1_out, Reset);
  not not_2 (not_2_out, Enable);
  Multiplexer #(.enable("false"), .select(2), .width(8)) multiplexer_1 (
    .in0(8'h1), .in1(8'h1f), .in2(8'h3f), .in3(8'h7f), .out(multiplexer_1_out), .sel(Rate));
  and and_1 (and_1_out, not_1_out, Clk);
  Counter #(.ongoal("load")) counter_1 (
    .clr(and_1_out), .up(not_2_out), .clk(Clk), .D(multiplexer_1_out), .Q(counter_1_q));  // open: load, count, carry
  nor nor_1 (DivOut, counter_1_q[0], counter_1_q[1], counter_1_q[2], counter_1_q[3], counter_1_q[4], counter_1_q[5], counter_1_q[6], counter_1_q[7]);
endmodule

module MORSE_LUT (
  input  [2:0] Char,
  output [13:0] MorseCode
);

  Multiplexer #(.enable("false"), .select(3), .width(14)) multiplexer_1 (
    .in0(14'h2a00), .in1(14'h3800), .in2(14'h2b80), .in3(14'h2ae0), .in4(14'h2ee0), .in5(14'h3ab8),
    .in6(14'h3aee), .in7(14'h3ba8), .out(MorseCode), .sel(Char));
endmodule

module demo_rate_divider (
  input  Reset,
  input  Enable,
  input  R1,
  input  R0
);

  wire clock_1_out, counter4_1_q0, counter4_1_q1, counter4_1_q2, counter4_1_q3, counter4_2_q0, counter4_2_q1,
       counter4_2_q2, counter4_2_q3, hex_decoder_1_s0, hex_decoder_1_s1, hex_decoder_1_s2, hex_decoder_1_s3,
       hex_decoder_1_s4, hex_decoder_1_s5, hex_decoder_1_s6, hex_decoder_2_s0, hex_decoder_2_s1,
       hex_decoder_2_s2, hex_decoder_2_s3, hex_decoder_2_s4, hex_decoder_2_s5, hex_decoder_2_s6,
       rate_divider_1_divout;

  Clock clock_1 (.out(clock_1_out));
  rate_divider rate_divider_1 (
    .Reset(Reset), .Enable(Enable), .Clk(clock_1_out), .Rate({R1, R0}), .DivOut(rate_divider_1_divout));
  counter4 counter4_1 (
    .enable(Enable), .Clk(rate_divider_1_divout), .clear_b(Reset), .Q3(counter4_1_q3), .Q2(counter4_1_q2),
    .Q1(counter4_1_q1), .Q0(counter4_1_q0));
  counter4 counter4_2 (
    .enable(Enable), .Clk(clock_1_out), .clear_b(Reset), .Q3(counter4_2_q3), .Q2(counter4_2_q2),
    .Q1(counter4_2_q1), .Q0(counter4_2_q0));
  HEX_DECODER hex_decoder_1 (
    .D3(counter4_1_q3), .D2(counter4_1_q2), .D1(counter4_1_q1), .D0(counter4_1_q0), .S0(hex_decoder_1_s0),
    .S1(hex_decoder_1_s1), .S2(hex_decoder_1_s2), .S3(hex_decoder_1_s3), .S4(hex_decoder_1_s4),
    .S5(hex_decoder_1_s5), .S6(hex_decoder_1_s6));
  HEX_DECODER hex_decoder_2 (
    .D3(counter4_2_q3), .D2(counter4_2_q2), .D1(counter4_2_q1), .D0(counter4_2_q0), .S0(hex_decoder_2_s0),
    .S1(hex_decoder_2_s1), .S2(hex_decoder_2_s2), .S3(hex_decoder_2_s3), .S4(hex_decoder_2_s4),
    .S5(hex_decoder_2_s5), .S6(hex_decoder_2_s6));
  _7_Segment_Display u_7_segment_display_1 (
    .g(hex_decoder_2_s6), .f(hex_decoder_2_s5), .a(hex_decoder_2_s0), .b(hex_decoder_2_s1),
    .e(hex_decoder_2_s4), .d(hex_decoder_2_s3), .c(hex_decoder_2_s2));  // open: dp
  _7_Segment_Display u_7_segment_display_2 (
    .g(hex_decoder_1_s6), .f(hex_decoder_1_s5), .a(hex_decoder_1_s0), .b(hex_decoder_1_s1),
    .e(hex_decoder_1_s4), .d(hex_decoder_1_s3), .c(hex_decoder_1_s2));  // open: dp
endmodule

module morse_code (
  input  [1:0] in_1,
  input  Enable,
  input  LoadEnable,
  input  [2:0] CharSelect
);

  wire clock_1_out, rate_divider_1_divout;
  wire [13:0] morse_lut_1_morsecode;

  Clock clock_1 (.out(clock_1_out));
  MORSE_LUT morse_lut_1 (.Char(CharSelect), .MorseCode(morse_lut_1_morsecode));
  rate_divider rate_divider_1 (
    .Enable(Enable), .Clk(clock_1_out), .Rate(in_1), .DivOut(rate_divider_1_divout));  // open: Reset
  // Shift_Register #(.length(14)) shift_register_1: pin names not known; wires that end beside it: LoadEnable, rate_divider_1_divout, morse_lut_1_morsecode[0], morse_lut_1_morsecode[1], morse_lut_1_morsecode[2], morse_lut_1_morsecode[3], morse_lut_1_morsecode[4], morse_lut_1_morsecode[5], morse_lut_1_morsecode[6], morse_lut_1_morsecode[7], morse_lut_1_morsecode[8], morse_lut_1_morsecode[9], morse_lut_1_morsecode[10], morse_lut_1_morsecode[11]
  LED led_1 ();  // open: in
endmodule
