// Logisim project lab6_part1.circ as structural Verilog: 14 circuits, main circuit part_1_state_table
module part_1_state_table (
  input  [2:0] curr_state,
  input  w,
  output [2:0] next_state
);

  wire and_1_out, and_2_out, and_3_out, multiplexer_1_out, multiplexer_2_out, not_1_out, not_2_out,
       not_3_out, not_4_out, or_1_out, or_2_out, or_4_out;

  not not_1 (not_1_out, curr_state[0]);
  not not_2 (not_2_out, curr_state[0]);
  not not_3 (not_3_out, curr_state[2]);
  or or_1 (or_1_out, curr_state[0], not_3_out);
  and and_1 (and_1_out, not_2_out, not_3_out);
  Multiplexer #(.enable("false")) multiplexer_1 (
    .in0(curr_state[0]), .in1(curr_state[2]), .out(multiplexer_1_out), .sel(w));
  not not_4 (not_4_out, curr_state[1]);
  and and_2 (and_2_out, curr_state[0], w);
  or or_2 (or_2_out, and_1_out, multiplexer_1_out);
  and and_3 (and_3_out, curr_state[1], or_1_out);
  and and_4 (next_state[2], curr_state[1], or_2_out);
  or or_3 (next_state[1], and_2_out, and_3_out);
  Multiplexer #(.enable("false")) multiplexer_2 (
    .in0(not_4_out), .in1(1'b1), .out(multiplexer_2_out), .sel(curr_state[2]));
  or or_4 (or_4_out, not_1_out, multiplexer_2_out);
  and and_5 (next_state[0], or_4_out, w);

  // Notes on the sheet:
  //   This is the state table, refer to the state diagram. To be completed by you. 
endmodule

module part_1_FSM (
  input  W,
  input  Enable,
  input  Reset,
  output z
);

  wire Clk_out;
  wire [2:0] part_1_state_table_1_next_state, state_q;

  part_1_state_table part_1_state_table_1 (.curr_state(state_q), .w(W), .next_state(part_1_state_table_1_next_state));
  Register #(.width(3)) state (
    .D(part_1_state_table_1_next_state), .en(Enable), .clk(Clk_out), .Q(state_q), .clr(Reset));
  Clock Clk (.out(Clk_out));
  and and_1 (z, state_q[0], state_q[2]);

  // Notes on the sheet:
  //   your state table
  //   state register
  //   output logic (to be completed by you)
endmodule

module part_2_ALU (
  input  [7:0] input_1,
  input  [7:0] input_2,
  input  ALU_op,
  output [7:0] ALU_out
);

  wire [7:0] adder_1_out, multiplier_1_out;

  Adder adder_1 (.a(input_1), .b(input_2), .out(adder_1_out));  // open: cin, cout
  Multiplier multiplier_1 (.a(input_1), .b(input_2), .out(multiplier_1_out));  // open: cin, cout
  Multiplexer #(.enable("false"), .width(8)) multiplexer_1 (
    .in0(adder_1_out), .in1(multiplier_1_out), .out(ALU_out), .sel(ALU_op));
endmodule

module part_2_state_table (
  input  [3:0] state,
  output ld_a,
  output ld_b,
  output ld_c,
  output ld_x,
  output [1:0] alu_select_a,
  output [1:0] alu_select_b,
  output ld_alu_out,
  output alu_op,
  output ld_r,
  output [3:0] next_state
);

  part_2_ld_a_state_table part_2_ld_a_state_table_1 (.state(state), .ld_a(ld_a));
  part_2_ld_b_state_table part_2_ld_b_state_table_1 (.state(state), .ld_b(ld_b));
  part_2_ld_c_state_table part_2_ld_c_state_table_1 (.state(state), .ld_c(ld_c));
  part_2_ld_x_state_table part_2_ld_x_state_table_1 (.state(state), .ld_x(ld_x));
  part_2_alu_select_a_state_table part_2_alu_select_a_state_table_1 (.state(state), .alu_select_a(alu_select_a));
  part_2_alu_select_b_state_table part_2_alu_select_b_state_table_1 (.state(state), .alu_select_b(alu_select_b));
  part_2_ld_alu_out_state_table part_2_ld_alu_out_state_table_1 (.state(state), .ld_alu_out(ld_alu_out));
  part_2_alu_op_state_table part_2_alu_op_state_table_1 (.state(state), .alu_op(alu_op));
  part_2_ld_r_state_table part_2_ld_r_state_table_1 (.state(state), .ld_r(ld_r));
  part_2_next_state part_2_next_state_1 (.state(state), .next_state(next_state));
endmodule

module part_2_ld_a_state_table (
  input  [3:0] state,
  output ld_a
);

  wire and_1_out, and_2_out, not_1_out, not_2_out, not_3_out, not_4_out, not_5_out, not_6_out;

  not not_1 (not_1_out, state[3]);
  not not_2 (not_2_out, state[2]);
  not not_3 (not_3_out, state[1]);
  not not_4 (not_4_out, state[3]);
  not not_5 (not_5_out, state[2]);
  not not_6 (not_6_out, state[0]);
  and and_1 (and_1_out, not_1_out, not_2_out, not_3_out, state[0]);
  and and_2 (and_2_out, not_4_out, not_5_out, state[1], not_6_out);
  or or_1 (ld_a, and_1_out, and_2_out);
endmodule

module part_2_ld_b_state_table (
  input  [3:0] state,
  output ld_b
);

  wire not_1_out, not_2_out;

  not not_1 (not_1_out, state[2]);
  not not_2 (not_2_out, state[3]);
  and and_1 (ld_b, state[0], state[1], not_1_out, not_2_out);
endmodule

module part_2_ld_c_state_table (
  input  [3:0] state,
  output ld_c
);

  wire not_1_out, not_2_out, not_3_out, not_4_out;

  not not_1 (not_1_out, state[0]);
  not not_2 (not_2_out, state[1]);
  not not_3 (not_3_out, state[2]);
  not not_4 (not_4_out, state[3]);
  and and_1 (ld_c, not_1_out, not_2_out, not_3_out, not_4_out);
endmodule

module part_2_ld_x_state_table (
  input  [3:0] state,
  output ld_x
);


  assign ld_x = 1'b0;
endmodule

module part_2_alu_select_a_state_table (
  input  [3:0] state,
  output [1:0] alu_select_a
);


  assign alu_select_a = 2'b00;
endmodule

module part_2_alu_select_b_state_table (
  input  [3:0] state,
  output [1:0] alu_select_b
);

  wire not_1_out, not_2_out, not_3_out, not_4_out, not_5_out;

  not not_1 (not_1_out, state[0]);
  not not_2 (not_2_out, state[1]);
  not not_3 (not_3_out, state[3]);
  not not_4 (not_4_out, state[2]);
  not not_5 (not_5_out, state[3]);
  and and_1 (alu_select_b[0], not_1_out, not_2_out, state[2], not_3_out);
  and and_2 (alu_select_b[1], state[0], state[1], not_4_out, not_5_out);
endmodule

module part_2_ld_alu_out_state_table (
  input  [3:0] state,
  output ld_alu_out
);

  wire and_1_out, and_2_out, not_1_out, not_2_out, not_3_out, not_4_out, not_5_out;

  not not_1 (not_1_out, state[0]);
  not not_2 (not_2_out, state[2]);
  not not_3 (not_3_out, state[3]);
  not not_4 (not_4_out, state[2]);
  not not_5 (not_5_out, state[3]);
  and and_1 (and_1_out, not_1_out, state[1], not_2_out, not_3_out);
  and and_2 (and_2_out, state[0], state[1], not_4_out, not_5_out);
  or or_1 (ld_alu_out, and_1_out, and_2_out);
endmodule

module part_2_alu_op_state_table (
  input  [3:0] state,
  output alu_op
);

  wire not_1_out, not_2_out, not_3_out;

  not not_1 (not_1_out, state[2]);
  not not_2 (not_2_out, state[0]);
  not not_3 (not_3_out, state[3]);
  and and_1 (alu_op, not_2_out, state[1], not_1_out, not_3_out);
endmodule

module part_2_ld_r_state_table (
  input  [3:0] state,
  output ld_r
);

  wire not_1_out, not_2_out, not_3_out;

  not not_1 (not_1_out, state[0]);
  not not_2 (not_2_out, state[1]);
  not not_3 (not_3_out, state[3]);
  and and_1 (ld_r, not_1_out, not_2_out, state[2], not_3_out);
endmodule

module part_2_next_state (
  input  [3:0] state,
  output [3:0] next_state
);

  wire and_1_out, and_2_out, and_3_out, and_4_out, not_1_out, not_2_out, not_3_out, not_4_out, not_5_out,
       not_6_out, not_7_out, not_8_out, not_9_out, not_10_out, not_11_out, not_12_out, not_13_out,
       not_14_out, not_15_out;

  not not_1 (not_1_out, state[0]);
  not not_2 (not_2_out, state[1]);
  not not_3 (not_3_out, state[2]);
  not not_4 (not_4_out, state[3]);
  not not_5 (not_5_out, state[0]);
  not not_6 (not_6_out, state[2]);
  not not_7 (not_7_out, state[3]);
  not not_8 (not_8_out, state[1]);
  not not_9 (not_9_out, state[2]);
  not not_10 (not_10_out, state[3]);
  not not_11 (not_11_out, state[0]);
  not not_12 (not_12_out, state[2]);
  not not_13 (not_13_out, state[3]);
  not not_14 (not_14_out, state[2]);
  not not_15 (not_15_out, state[3]);
  and and_1 (and_1_out, not_1_out, not_2_out, not_3_out, not_4_out);
  and and_2 (and_2_out, not_5_out, state[1], not_6_out, not_7_out);
  and and_3 (and_3_out, state[0], not_8_out, not_9_out, not_10_out);
  and and_4 (and_4_out, not_11_out, state[1], not_12_out, not_13_out);
  and and_5 (next_state[2], state[0], state[1], not_14_out, not_15_out);
  or or_1 (next_state[0], and_1_out, and_2_out);
  or or_2 (next_state[1], and_3_out, and_4_out);

  assign next_state[3] = 1'b0;
endmodule
