// Logisim project lab7_part2.circ as structural Verilog: 3 circuits, main circuit main
module main (
  input  Enable,
  input  Reset,
  input  [23:0] DataIn,
  input  [6:0] X,
  input  [6:0] Y
);

  wire and_1_out, clk_out;
  wire [6:0] fsm_1_xout, fsm_1_yout;

  Clock clk (.out(clk_out));
  and and_1 (and_1_out, Reset, clk_out);
  FSM fsm_1 (.Reset(and_1_out), .En(Enable), .clk(clk_out), .X(X), .Y(Y), .Xout(fsm_1_xout), .Yout(fsm_1_yout));
  // RGB_Video rgb_video_1: pin names not known; wires that end beside it: and_1_out, clk_out, Enable, fsm_1_xout, fsm_1_yout, DataIn
endmodule

module FSM (
  input  Reset,
  input  En,
  input  clk,
  input  [6:0] X,
  input  [6:0] Y,
  output [6:0] Xout,
  output [6:0] Yout
);

  wire and_1_out;
  wire [7:0] counter_1_q;

  and and_1 (and_1_out, En, clk);
  Counter counter_1 (.clr(Reset), .clk(and_1_out), .Q(counter_1_q));  // open: load, up, count, D, carry
  Datapath datapath_1 (
    .clk(clk), .Reset(Reset), .EN(En), .X_add(counter_1_q[3:0]), .Y_add(counter_1_q[7:4]), .X(X), .Y(Y),
    .Xout(Xout), .Yout(Yout));
endmodule

module Datapath (
  input  clk,
  input  Reset,
  input  EN,
  input  [3:0] X_add,
  input  [3:0] Y_add,
  input  [6:0] X,
  input  [6:0] Y,
  output [6:0] Xout,
  output [6:0] Yout
);

  wire and_1_out;
  wire [6:0] adder_1_out, adder_2_out, bit_extender_1_out, bit_extender_2_out;

  assign bit_extender_1_out = {{3{1'b0}}, X_add};  // Bit_Extender bit_extender_1
  assign bit_extender_2_out = {{3{1'b0}}, Y_add};  // Bit_Extender bit_extender_2
  Adder #(.width(7)) adder_1 (.a(bit_extender_2_out), .b(Y), .out(adder_1_out));  // open: cin, cout
  and and_1 (and_1_out, clk, Reset);
  Adder #(.width(7)) adder_2 (.a(bit_extender_1_out), .b(X), .out(adder_2_out));  // open: cin, cout
  Register #(.width(7)) register_1 (.D(adder_2_out), .en(EN), .clk(clk), .Q(Xout), .clr(and_1_out));
  Register #(.width(7)) register_2 (.D(adder_1_out), .en(EN), .clk(clk), .Q(Yout), .clr(and_1_out));
endmodule
